// Logisim project Proyecto.circ as structural Verilog: 12 circuits, main circuit main
module main (
  input  w,
  input  x,
  input  y,
  input  z,
  input  w_2,
  input  x_2,
  input  y_2,
  input  z_2
);

  wire Decodificador_2_out_5, Decodificador_2_out_6, Decodificador_2_out_7, Decodificador_2_out_8,
       Decodificador_2_out_9, Decodificador_2_out_10, Decodificador_2_out_11, Decodificador_3_out_5,
       Decodificador_3_out_6, Decodificador_3_out_7, Decodificador_3_out_8, Decodificador_3_out_9,
       Decodificador_3_out_10, Decodificador_3_out_11, Decodificador_out_5, Decodificador_out_6,
       Decodificador_out_7, Decodificador_out_8, Decodificador_out_9, Decodificador_out_10,
       Decodificador_out_11, sumador_1_s0, sumador_1_s1, sumador_1_s2, sumador_1_s3;

  Decodificador Decodificador (
    .w(w_2), .x(x_2), .y(y_2), .z(z_2), .out_5(Decodificador_out_5), .out_6(Decodificador_out_6),
    .out_7(Decodificador_out_7), .out_8(Decodificador_out_8), .out_9(Decodificador_out_9),
    .out_10(Decodificador_out_10), .out_11(Decodificador_out_11));
  Decodificador Decodificador_2 (
    .w(w), .x(x), .y(y), .z(z), .out_5(Decodificador_2_out_5), .out_6(Decodificador_2_out_6),
    .out_7(Decodificador_2_out_7), .out_8(Decodificador_2_out_8), .out_9(Decodificador_2_out_9),
    .out_10(Decodificador_2_out_10), .out_11(Decodificador_2_out_11));
  Sumador sumador_1 (
    .W1(x_2), .W2(y_2), .W3(z_2), .W0(w_2), .X0(w), .X1(x), .X2(y), .X3(z), .S0(sumador_1_s0),
    .S1(sumador_1_s1), .S2(sumador_1_s2), .S3(sumador_1_s3));  // open: S4
  _7_Segment_Display u_7_segment_display_1 (
    .g(Decodificador_2_out_11), .f(Decodificador_2_out_10), .a(Decodificador_2_out_5),
    .b(Decodificador_2_out_6), .e(Decodificador_2_out_9), .d(Decodificador_2_out_8), .c(Decodificador_2_out_7));  // open: dp
  _7_Segment_Display u_7_segment_display_2 (
    .g(Decodificador_out_11), .f(Decodificador_out_10), .a(Decodificador_out_5), .b(Decodificador_out_6),
    .e(Decodificador_out_9), .d(Decodificador_out_8), .c(Decodificador_out_7));  // open: dp
  Decodificador Decodificador_3 (
    .w(sumador_1_s0), .x(sumador_1_s1), .y(sumador_1_s2), .z(sumador_1_s3), .out_5(Decodificador_3_out_5),
    .out_6(Decodificador_3_out_6), .out_7(Decodificador_3_out_7), .out_8(Decodificador_3_out_8),
    .out_9(Decodificador_3_out_9), .out_10(Decodificador_3_out_10), .out_11(Decodificador_3_out_11));
  _7_Segment_Display u_7_segment_display_3 (
    .g(Decodificador_3_out_11), .f(Decodificador_3_out_10), .a(Decodificador_3_out_5),
    .b(Decodificador_3_out_6), .e(Decodificador_3_out_9), .d(Decodificador_3_out_8), .c(Decodificador_3_out_7));  // open: dp
endmodule

module Decodificador (
  input  w,
  input  x,
  input  y,
  input  z,
  output out_5,
  output out_6,
  output out_7,
  output out_8,
  output out_9,
  output out_10,
  output out_11
);

  segmento_a_0_9_normal segmento_a_0_9_normal_1 (.w(w), .x(x), .y(y), .z(z), .out_5(out_5));
  segmento_b_0_9_normal segmento_b_0_9_normal_1 (.w(w), .x(x), .y(y), .z(z), .out_5(out_6));
  segmento_c_0_9_normal segmento_c_0_9_normal_1 (.w(w), .x(x), .y(y), .z(z), .out_5(out_7));
  segmento_d_0_9_normal segmento_d_0_9_normal_1 (.w(w), .x(x), .y(y), .z(z), .out_5(out_8));
  segmento_e_0_9_normal segmento_e_0_9_normal_1 (.w(w), .x(x), .y(y), .z(z), .out_5(out_9));
  segmento_f_0_9_normal segmento_f_0_9_normal_1 (.w(w), .x(x), .y(y), .z(z), .out_5(out_10));
  segmento_g_0_9_normal segmento_g_0_9_normal_1 (.w(w), .x(x), .y(y), .z(z), .out_5(out_11));
endmodule

// A
module segmento_a_0_9_normal (
  input  w,
  input  x,
  input  y,
  input  z,
  output out_5
);

  wire not_1_out, not_2_out, not_3_out, not_4_out, or_1_out, or_2_out, w_prime_x_out, w_prime_xz_out,
       w_prime_y_out, wx_prime_out, wx_prime_y_prime_out, x_prime_y_prime_out, x_prime_y_prime_z_prime_out;

  not not_1 (not_1_out, w);
  and w_prime_y (w_prime_y_out, not_1_out, y);
  and w_prime_x (w_prime_x_out, not_1_out, x);
  not not_2 (not_2_out, x);
  and w_prime_xz (w_prime_xz_out, w_prime_x_out, z);
  and wx_prime (wx_prime_out, w, not_2_out);
  not not_3 (not_3_out, y);
  not not_4 (not_4_out, z);
  or or_1 (or_1_out, w_prime_y_out, w_prime_xz_out);
  and wx_prime_y_prime (wx_prime_y_prime_out, wx_prime_out, not_3_out);
  and x_prime_y_prime (x_prime_y_prime_out, not_3_out, not_2_out);
  and x_prime_y_prime_z_prime (x_prime_y_prime_z_prime_out, x_prime_y_prime_out, not_4_out);
  or or_2 (or_2_out, wx_prime_y_prime_out, x_prime_y_prime_z_prime_out);
  or or_3 (out_5, or_1_out, or_2_out);
endmodule

// B
module segmento_b_0_9_normal (
  input  w,
  input  x,
  input  y,
  input  z,
  output out_5
);

  wire not_1_out, not_2_out, not_3_out, not_4_out, or_1_out, or_3_out, w_prime_x_prime_out,
       w_prime_x_prime_y_out, w_prime_y_out, w_prime_y_prime_out, w_prime_y_prime_z_prime_out,
       w_prime_yz_out, x_prime_y_prime_out;

  not not_1 (not_1_out, w);
  not not_2 (not_2_out, x);
  not not_3 (not_3_out, y);
  not not_4 (not_4_out, z);
  and w_prime_y_prime (w_prime_y_prime_out, not_1_out, not_3_out);
  and x_prime_y_prime (x_prime_y_prime_out, not_2_out, not_3_out);
  and w_prime_y_prime_z_prime (w_prime_y_prime_z_prime_out, w_prime_y_prime_out, not_4_out);
  and w_prime_y (w_prime_y_out, y, not_1_out);
  and w_prime_x_prime (w_prime_x_prime_out, not_2_out, not_1_out);
  and w_prime_yz (w_prime_yz_out, w_prime_y_out, z);
  and w_prime_x_prime_y (w_prime_x_prime_y_out, w_prime_x_prime_out, y);
  or or_1 (or_1_out, w_prime_y_prime_z_prime_out, x_prime_y_prime_out);
  or or_2 (out_5, or_1_out, or_3_out);
  or or_3 (or_3_out, w_prime_yz_out, w_prime_x_prime_y_out);
endmodule

// C
module segmento_c_0_9_normal (
  input  w,
  input  x,
  input  y,
  input  z,
  output out_5
);

  wire not_1_out, not_2_out, not_3_out, or_1_out, or_2_out, w_prime_x_out, w_prime_xy_out, w_prime_y_out,
       w_prime_y_prime_out, w_prime_yz_out, x_prime_y_prime_out;

  not not_1 (not_1_out, w);
  not not_2 (not_2_out, x);
  not not_3 (not_3_out, y);
  and w_prime_y_prime (w_prime_y_prime_out, not_1_out, not_3_out);
  and x_prime_y_prime (x_prime_y_prime_out, not_3_out, not_2_out);
  and w_prime_y (w_prime_y_out, not_1_out, y);
  and w_prime_yz (w_prime_yz_out, w_prime_y_out, z);
  and w_prime_x (w_prime_x_out, not_1_out, x);
  or or_1 (or_1_out, w_prime_y_prime_out, x_prime_y_prime_out);
  and w_prime_xy (w_prime_xy_out, w_prime_x_out, y);
  or or_2 (or_2_out, w_prime_yz_out, w_prime_xy_out);
  or or_3 (out_5, or_1_out, or_2_out);
endmodule

// D
module segmento_d_0_9_normal (
  input  w,
  input  x,
  input  y,
  input  z,
  output out_5
);

  wire not_1_out, not_2_out, not_3_out, not_4_out, or_1_out, or_2_out, or_3_out, w_prime_x_out,
       w_prime_x_prime_out, w_prime_x_prime_y_out, w_prime_xy_prime_out, w_prime_xy_prime_z_out,
       w_prime_y_out, w_prime_yz_prime_out, wx_prime_out, wx_prime_y_prime_out, x_prime_y_prime_out,
       x_prime_y_prime_z_prime_out;

  not not_1 (not_1_out, x);
  not not_2 (not_2_out, y);
  not not_3 (not_3_out, z);
  not not_4 (not_4_out, w);
  and wx_prime (wx_prime_out, w, not_1_out);
  and x_prime_y_prime (x_prime_y_prime_out, not_1_out, not_2_out);
  and wx_prime_y_prime (wx_prime_y_prime_out, wx_prime_out, not_2_out);
  and x_prime_y_prime_z_prime (x_prime_y_prime_z_prime_out, x_prime_y_prime_out, not_3_out);
  and w_prime_x_prime (w_prime_x_prime_out, not_1_out, not_4_out);
  and w_prime_x_prime_y (w_prime_x_prime_y_out, w_prime_x_prime_out, y);
  and w_prime_y (w_prime_y_out, not_4_out, y);
  and w_prime_x (w_prime_x_out, not_4_out, x);
  or or_1 (or_1_out, wx_prime_y_prime_out, x_prime_y_prime_z_prime_out);
  and w_prime_yz_prime (w_prime_yz_prime_out, w_prime_y_out, not_3_out);
  and w_prime_xy_prime (w_prime_xy_prime_out, w_prime_x_out, not_2_out);
  or or_2 (or_2_out, w_prime_x_prime_y_out, w_prime_yz_prime_out);
  and w_prime_xy_prime_z (w_prime_xy_prime_z_out, w_prime_xy_prime_out, z);
  or or_3 (or_3_out, or_1_out, or_2_out);
  or or_4 (out_5, or_3_out, w_prime_xy_prime_z_out);
endmodule

// E
module segmento_e_0_9_normal (
  input  w,
  input  x,
  input  y,
  input  z,
  output out_5
);

  wire not_1_out, not_2_out, not_3_out, not_4_out, w_prime_y_out, w_prime_yz_prime_out, x_prime_y_prime_out,
       x_prime_y_prime_z_prime_out;

  not not_1 (not_1_out, w);
  not not_2 (not_2_out, x);
  not not_3 (not_3_out, y);
  not not_4 (not_4_out, z);
  and w_prime_y (w_prime_y_out, not_1_out, y);
  and x_prime_y_prime (x_prime_y_prime_out, not_2_out, not_3_out);
  and x_prime_y_prime_z_prime (x_prime_y_prime_z_prime_out, x_prime_y_prime_out, not_4_out);
  and w_prime_yz_prime (w_prime_yz_prime_out, w_prime_y_out, not_4_out);
  or or_1 (out_5, w_prime_yz_prime_out, x_prime_y_prime_z_prime_out);
endmodule

// F
module segmento_f_0_9_normal (
  input  w,
  input  x,
  input  y,
  input  z,
  output out_5
);

  wire not_1_out, not_2_out, not_3_out, not_4_out, or_1_out, or_2_out, w_prime_x_2_out, w_prime_x_out,
       w_prime_xy_prime_out, w_prime_xz_prime_out, wx_prime_out, wx_prime_y_prime_out, x_prime_y_prime_out,
       x_prime_y_prime_z_prime_out;

  not not_1 (not_1_out, w);
  not not_2 (not_2_out, x);
  not not_3 (not_3_out, y);
  not not_4 (not_4_out, z);
  and w_prime_x (w_prime_x_out, not_1_out, x);
  and w_prime_xy_prime (w_prime_xy_prime_out, w_prime_x_out, not_3_out);
  and x_prime_y_prime (x_prime_y_prime_out, not_2_out, not_3_out);
  and w_prime_x_2 (w_prime_x_2_out, not_1_out, x);
  and x_prime_y_prime_z_prime (x_prime_y_prime_z_prime_out, x_prime_y_prime_out, not_4_out);
  and wx_prime (wx_prime_out, not_2_out, w);
  and wx_prime_y_prime (wx_prime_y_prime_out, wx_prime_out, not_3_out);
  and w_prime_xz_prime (w_prime_xz_prime_out, not_4_out, w_prime_x_2_out);
  or or_1 (or_1_out, w_prime_xy_prime_out, x_prime_y_prime_z_prime_out);
  or or_2 (or_2_out, wx_prime_y_prime_out, w_prime_xz_prime_out);
  or or_3 (out_5, or_1_out, or_2_out);
endmodule

// G
module segmento_g_0_9_normal (
  input  w,
  input  x,
  input  y,
  input  z,
  output out_5
);

  wire not_1_out, not_2_out, not_3_out, not_4_out, or_1_out, or_2_out, w_prime_x_out, w_prime_x_prime_out,
       w_prime_x_prime_y_out, w_prime_xy_prime_out, w_prime_y_out, w_prime_yz_prime_out, wx_prime_out,
       wx_prime_y_prime_out;

  not not_1 (not_1_out, w);
  not not_2 (not_2_out, x);
  not not_3 (not_3_out, y);
  not not_4 (not_4_out, z);
  and w_prime_x (w_prime_x_out, not_1_out, x);
  and w_prime_xy_prime (w_prime_xy_prime_out, w_prime_x_out, not_3_out);
  and w_prime_x_prime (w_prime_x_prime_out, not_1_out, not_2_out);
  and wx_prime (wx_prime_out, not_2_out, w);
  and w_prime_x_prime_y (w_prime_x_prime_y_out, w_prime_x_prime_out, y);
  and w_prime_y (w_prime_y_out, not_1_out, y);
  and wx_prime_y_prime (wx_prime_y_prime_out, wx_prime_out, not_3_out);
  and w_prime_yz_prime (w_prime_yz_prime_out, not_4_out, w_prime_y_out);
  or or_1 (or_1_out, w_prime_xy_prime_out, wx_prime_y_prime_out);
  or or_2 (or_2_out, w_prime_x_prime_y_out, w_prime_yz_prime_out);
  or or_3 (out_5, or_1_out, or_2_out);
endmodule

module Medio_Sumador (
  input  w,
  input  x,
  output S,
  output Count
);

  wire and_1_out, and_2_out, not_1_out, not_2_out;

  not not_1 (not_1_out, w);
  not not_2 (not_2_out, x);
  and and_1 (and_1_out, not_1_out, x);
  and and_2 (and_2_out, not_2_out, w);
  or \xor  (S, and_1_out, and_2_out);
  and and_3 (Count, w, x);
endmodule

// FA
module Sumador_Completo (
  input  W,
  input  X,
  input  Count,
  output S,
  output Count_2
);

  wire medio_sumador_1_count, medio_sumador_1_s, medio_sumador_2_count;

  Medio_Sumador medio_sumador_1 (.w(W), .x(X), .S(medio_sumador_1_s), .Count(medio_sumador_1_count));
  Medio_Sumador medio_sumador_2 (.w(Count), .x(medio_sumador_1_s), .S(S), .Count(medio_sumador_2_count));
  or or_1 (Count_2, medio_sumador_2_count, medio_sumador_1_count);
endmodule

module Sumador (
  input  W1,
  input  W2,
  input  W3,
  input  W0,
  input  X0,
  input  X1,
  input  X2,
  input  X3,
  output S0,
  output S1,
  output S2,
  output S3,
  output S4
);

  wire sumador_completo_1_count_2, sumador_completo_2_count_2, sumador_completo_3_count_2;

  Sumador_Completo sumador_completo_1 (.W(W0), .X(X0), .Count(1'b0), .S(S0), .Count_2(sumador_completo_1_count_2));
  Sumador_Completo sumador_completo_2 (
    .W(W1), .X(X1), .Count(sumador_completo_1_count_2), .S(S1), .Count_2(sumador_completo_2_count_2));
  Sumador_Completo sumador_completo_3 (
    .W(W2), .X(X2), .Count(sumador_completo_2_count_2), .S(S2), .Count_2(sumador_completo_3_count_2));
  Sumador_Completo sumador_completo_4 (.W(W3), .X(X3), .Count(sumador_completo_3_count_2), .S(S3), .Count_2(S4));
endmodule
